# Fritzing sketch wiring_diagram_v2_fritzing (saved by Fritzing 0.9.3b)

parts:
  Raspberry_Pi_1 = Raspberry Pi 3 [part_number=RPI-3-V1.2]
  LED1 = LED - 5mm [color="Green (565nm)" package="5 mm [THT]"]
  S1 = Round Pushbutton
  Part1 = Thermal Printer
  Power_plug1 = Power plug

nets:
  N1: Raspberry_Pi_1.GPIO24, LED1.anode
  N2: Raspberry_Pi_1.GPIO23, S1.leg1
  N3: Raspberry_Pi_1.GND, LED1.cathode, S1.leg0, Part1.GND#2
  N4: Raspberry_Pi_1.GPIO14, Part1.RXD
  N5: Part1.GND#0, Power_plug1.GND
  N6: Part1.VH, Power_plug1.VCC

notes:
  9V 2A DC
  Power supply
